# Fritzing sketch 01_temp_sensor (saved by Fritzing 0.9.6b)

parts:
  Part1 = Arduino Uno (Rev3) - ICSP
  DS1 = DS18B20 1-Wire Temperature Sensor Probe Cable

nets:
  GND: Part1.GND, DS1.GND
  N1: Part1.D2, DS1.shield
  5V: Part1.5V, DS1.VDD
