# Fritzing sketch 02_rfid_reader (saved by Fritzing 0.9.6b)

parts:
  Part2 = Arduino Uno (Rev3) - ICSP
  DS2 = DS18B20 1-Wire Temperature Sensor Probe Cable
  Part3 = RFID-RC522-v2

nets:
  N1: Part2.ICSP_MISO, Part2.D12/MISO, Part3.MISO
  N2: Part2.D9_PWM, Part3.RST
  N3: Part2.D10_PWM/SS, Part3.SDA
  N4: Part2.D11_PWM/MOSI, Part3.MOSI
  N5: Part2.D13/SCK, Part3.SCK
  GND: Part2.GND, DS2.GND, Part3.GND
  N6: Part2.D2, DS2.shield
  3V3: Part2.3V3, Part3.3.3V
  5V: Part2.5V, DS2.VDD

custom parts:
  RFID-RC522-v2: A simple China made RFID-RC522 Reader; do check the pin labels, as this is a MFRC522 based clone.
