# Fritzing sketch 02_servo (saved by Fritzing 0.9.6b)

parts:
  Part1 = Arduino Uno (Rev3) - ICSP
  Part2 = LCD1602-I2C
  J1 = Basic Servo

nets:
  N1: Part1.D9_PWM, J1.pulse
  N2: Part1.A4/SDA, Part2.SDA
  N3: Part1.A5/SCL, Part2.SCL
  5V: Part1.5V, Part2.VCC
  GND: Part1.GND, Part2.GND, J1.gnd
  VIN: Part1.VIN, J1.vcc

custom parts:
  LCD1602-I2C: A standard character display, usually with 2x16 characters. Comes in many colors with LCM1602 IIC attached.
