# Fritzing sketch 01_beagblebone_sos (saved by Fritzing 0.9.6b)
breadboards: 1

parts:
  BeagleBone1 = BeagleBone Black
  R1 = Resistor [tolerance=±5% resistance=100 power=0.25 package="1206 [SMD]"]
  LED1 = LED - 5mm [color="Red (633nm)" current=0.030 package="5 mm [THT]"]

nets:
  N1: BeagleBone1.no_name_yet#108, BeagleBone1.no_name_yet#110, LED1.anode
  N2: R1.Pin_1, LED1.cathode

custom parts:
  BeagleBone Black: BeagleBone Black rev. A5B
