# Fritzing sketch 01_dht11 (saved by Fritzing 0.9.6b)
breadboards: 1

parts:
  BeagleBone1 = BeagleBone Black
  DHT1 = DHT11 Humitidy and Temperature Sensor
  R1 = Resistor [tolerance=±5% power=0.25 resistance=220 package=THT]

nets:
  N1: BeagleBone1.no_name_yet#1, DHT1.GND
  N2: BeagleBone1.no_name_yet#3, DHT1.VDD, R1.Pin_1
  N3: BeagleBone1.no_name_yet#110, DHT1.DATA, R1.Pin_0

custom parts:
  BeagleBone Black: BeagleBone Black rev. A5B
  DHT11 Humitidy and Temperature Sensor: DHT11 Humidity and Temperature Sensor
