# Fritzing sketch 01_UART (saved by Fritzing 0.9.6b)

parts:
  Part1 = Arduino Uno (Rev3) - ICSP
  DS1 = DS18B20 1-Wire Temperature Sensor Probe Cable
  BeagleBone1 = BeagleBone Black

nets:
  GND: Part1.GND, DS1.GND, BeagleBone1.no_name_yet#1
  N1: Part1.D1/TX, BeagleBone1.no_name_yet#26
  N2: Part1.D2, DS1.shield
  5V: Part1.5V, DS1.VDD

custom parts:
  BeagleBone Black: BeagleBone Black rev. A5B
